# Fritzing sketch vibration motor circuit (saved by Fritzing 0.9.3b)
breadboards: 1

parts:
  Part1 = Arduino Uno (Rev3) - ICSP
  R1 = Resistor [tolerance=±5% resistance=1k package="2010 [SMD]"]
  D1 = P1000K [part_number=P1000K]
  Q1 = NPN-Transistor [package="TO92 [THT]"]
  U1 = Vibration Motor- ROB-08449 [package=vibe-motor-10mm]

nets:
  N1: Part1.D3_PWM, R1.Pin_0
  N2: Part1.3V3, D1.cathode, U1.+
  N3: Part1.GND, Q1.E
  N4: R1.Pin_1, Q1.C
  N5: D1.anode, Q1.B, U1.-
